// Logisim project Decode WB Stage.circ as structural Verilog: 9 circuits, main circuit main
module main (
  input  [31:0] ValM,
  input  [31:0] ValE,
  input  [3:0] icode,
  input  [3:0] rA,
  input  [3:0] rB,
  output [31:0] ValA,
  output [31:0] ValB,
  output [3:0] dstE,
  output [3:0] dstM,
  output [3:0] srcA,
  output [3:0] srcB
);

  wire clock_1_out;

  Clock clock_1 (.out(clock_1_out));
  Register_File register_file_1 (
    .W_Data___ValM(ValM), .W_Addr___DestM(dstM), .W_Data2___ValE(ValE), .W_Addr___DestE(dstE), .ValA(ValE),
    .ValB(ValB), .R_Addr___SrcB(srcB), .R_Addr___SrcA(srcA), .icode(icode), .Clock(clock_1_out));
  dstM dstm_1 (.out_3(dstM), .icode(icode), .rB(rA));
  dstE dste_1 (.out_3(dstE), .icode(icode), .rB(rB));
  srcA srca_1 (.out_3(srcA), .icode(icode), .rA(rA));
  srcB srcb_1 (.icode(icode), .out_3(srcB), .rB(rB));

  assign ValA = ValE;

  // Notes on the sheet:
  //   dstm and srca 0010
endmodule

// 8x32 Register File (2 read, 2 write)
module Register_File (
  input  [3:0] icode,
  input  Clock,
  input  [31:0] W_Data___ValM,
  input  [3:0] R_Addr___SrcA,
  input  [3:0] W_Addr___DestM,
  input  [3:0] R_Addr___SrcB,
  input  [31:0] W_Data2___ValE,
  input  [3:0] W_Addr___DestE,
  output [31:0] ValA,
  output [31:0] ValB
);

  wire and_1_out, and_2_out, and_3_out, or_1_out, register_helper_1_select, register_helper_2_select,
       register_helper_3_select, register_helper_4_select, register_helper_5_select,
       register_helper_6_select, register_helper_7_select, register_helper_8_select, write_decoder_1__0,
       write_decoder_1__1, write_decoder_1__2, write_decoder_1__3, write_decoder_1__4, write_decoder_1__5,
       write_decoder_1__6, write_decoder_1__7, write_decoder_2__0, write_decoder_2__1, write_decoder_2__2,
       write_decoder_2__3, write_decoder_2__4, write_decoder_2__5, write_decoder_2__6, write_decoder_2__7;
  wire [7:0] counter_1_q;
  wire [31:0] register_1_q, register_2_q, register_3_q, register_4_q, register_5_q, register_6_q,
       register_7_q, register_8_q, register_helper_1_data, register_helper_2_data, register_helper_3_data,
       register_helper_4_data, register_helper_5_data, register_helper_6_data, register_helper_7_data,
       register_helper_8_data;

  and and_1 (and_1_out, ~icode[0], ~icode[1], icode[2], ~icode[3]);  // AND_Gate
  Counter #(.max('h5)) counter_1 (.Q(counter_1_q), .clk(Clock));  // open: load, D, count, carry, clr
  Write_Decoder write_decoder_1 (
    .W_Addr(W_Addr___DestM), ._0(write_decoder_1__0), ._1(write_decoder_1__1), ._2(write_decoder_1__2),
    ._3(write_decoder_1__3), ._4(write_decoder_1__4), ._5(write_decoder_1__5), ._6(write_decoder_1__6),
    ._7(write_decoder_1__7));
  Write_Decoder write_decoder_2 (
    .W_Addr(W_Addr___DestE), ._0(write_decoder_2__0), ._1(write_decoder_2__1), ._2(write_decoder_2__2),
    ._3(write_decoder_2__3), ._4(write_decoder_2__4), ._5(write_decoder_2__5), ._6(write_decoder_2__6),
    ._7(write_decoder_2__7));
  and and_2 (and_2_out, ~counter_1_q[0], ~counter_1_q[1], counter_1_q[2], ~counter_1_q[3], and_1_out);  // AND_Gate
  and and_3 (and_3_out, counter_1_q[0], ~counter_1_q[1], counter_1_q[2], ~counter_1_q[3], ~and_1_out);  // AND_Gate
  or or_1 (or_1_out, and_3_out, and_2_out);
  Register_Helper register_helper_1 (
    .DataM(W_Data___ValM), .DataE(W_Data2___ValE), .Select_M(write_decoder_1__0),
    .Select_E(write_decoder_2__0), .Data(register_helper_1_data), .Select(register_helper_1_select));
  Register_Helper register_helper_2 (
    .DataM(W_Data___ValM), .DataE(W_Data2___ValE), .Select_M(write_decoder_1__1),
    .Select_E(write_decoder_2__1), .Data(register_helper_2_data), .Select(register_helper_2_select));
  Register_Helper register_helper_3 (
    .DataM(W_Data___ValM), .DataE(W_Data2___ValE), .Select_M(write_decoder_1__2),
    .Select_E(write_decoder_2__2), .Data(register_helper_3_data), .Select(register_helper_3_select));
  Register_Helper register_helper_4 (
    .DataM(W_Data___ValM), .DataE(W_Data2___ValE), .Select_M(write_decoder_1__3),
    .Select_E(write_decoder_2__3), .Data(register_helper_4_data), .Select(register_helper_4_select));
  Register_Helper register_helper_5 (
    .DataM(W_Data___ValM), .DataE(W_Data2___ValE), .Select_M(write_decoder_1__4),
    .Select_E(write_decoder_2__4), .Data(register_helper_5_data), .Select(register_helper_5_select));
  Register_Helper register_helper_6 (
    .DataM(W_Data___ValM), .DataE(W_Data2___ValE), .Select_M(write_decoder_1__5),
    .Select_E(write_decoder_2__5), .Data(register_helper_6_data), .Select(register_helper_6_select));
  Register_Helper register_helper_7 (
    .DataM(W_Data___ValM), .DataE(W_Data2___ValE), .Select_M(write_decoder_1__6),
    .Select_E(write_decoder_2__6), .Data(register_helper_7_data), .Select(register_helper_7_select));
  Register_Helper register_helper_8 (
    .DataM(W_Data___ValM), .DataE(W_Data2___ValE), .Select_M(write_decoder_1__7),
    .Select_E(write_decoder_2__7), .Data(register_helper_8_data), .Select(register_helper_8_select));
  Register #(.width(32)) register_1 (
    .D(register_helper_1_data), .en(register_helper_1_select), .Q(register_1_q), .clk(or_1_out));  // open: clr
  Register #(.width(32)) register_2 (
    .D(register_helper_2_data), .en(register_helper_2_select), .Q(register_2_q), .clk(or_1_out));  // open: clr
  Register #(.width(32)) register_3 (
    .D(register_helper_3_data), .en(register_helper_3_select), .Q(register_3_q), .clk(or_1_out));  // open: clr
  Register #(.width(32)) register_4 (
    .D(register_helper_4_data), .en(register_helper_4_select), .Q(register_4_q), .clk(or_1_out));  // open: clr
  Register #(.width(32)) register_5 (
    .D(register_helper_5_data), .en(register_helper_5_select), .Q(register_5_q), .clk(or_1_out));  // open: clr
  Register #(.width(32)) register_6 (
    .D(register_helper_6_data), .en(register_helper_6_select), .Q(register_6_q), .clk(or_1_out));  // open: clr
  Register #(.width(32)) register_7 (
    .D(register_helper_7_data), .en(register_helper_7_select), .Q(register_7_q), .clk(or_1_out));  // open: clr
  Register #(.width(32)) register_8 (
    .D(register_helper_8_data), .en(register_helper_8_select), .Q(register_8_q), .clk(or_1_out));  // open: clr
  Multiplexer #(.select(4), .width(32)) multiplexer_1 (
    .in0(register_1_q), .in1(register_2_q), .in2(register_3_q), .in3(register_4_q), .in4(register_5_q),
    .in5(register_6_q), .in6(register_7_q), .in7(register_8_q), .out(ValA), .sel(R_Addr___SrcA));  // open: in8, in9, in10, in11, in12, in13, in14, in15, en
  Multiplexer #(.select(4), .width(32)) multiplexer_2 (
    .in0(register_1_q), .in1(register_2_q), .in2(register_3_q), .in3(register_4_q), .in4(register_5_q),
    .in5(register_6_q), .in6(register_7_q), .in7(register_8_q), .out(ValB), .sel(R_Addr___SrcB));  // open: in8, in9, in10, in11, in12, in13, in14, in15, en
endmodule

module Write_Decoder (
  input  [3:0] W_Addr,
  output _0,
  output _1,
  output _2,
  output _3,
  output _4,
  output _5,
  output _6,
  output _7
);

  wire not_1_out, not_2_out, not_3_out, not_4_out, not_5_out, not_6_out, not_7_out, not_8_out, not_9_out,
       not_10_out, not_11_out, not_12_out, not_13_out, not_14_out, not_15_out, not_16_out, not_17_out,
       not_18_out, not_19_out, not_20_out;

  not not_1 (not_1_out, W_Addr[0]);
  not not_2 (not_2_out, W_Addr[1]);
  not not_3 (not_3_out, W_Addr[2]);
  not not_4 (not_4_out, W_Addr[3]);
  not not_5 (not_5_out, W_Addr[1]);
  not not_6 (not_6_out, W_Addr[2]);
  not not_7 (not_7_out, W_Addr[3]);
  not not_8 (not_8_out, W_Addr[0]);
  not not_9 (not_9_out, W_Addr[2]);
  not not_10 (not_10_out, W_Addr[3]);
  not not_11 (not_11_out, W_Addr[2]);
  not not_12 (not_12_out, W_Addr[3]);
  not not_13 (not_13_out, W_Addr[0]);
  not not_14 (not_14_out, W_Addr[1]);
  not not_15 (not_15_out, W_Addr[3]);
  not not_16 (not_16_out, W_Addr[1]);
  not not_17 (not_17_out, W_Addr[3]);
  not not_18 (not_18_out, W_Addr[0]);
  not not_19 (not_19_out, W_Addr[3]);
  not not_20 (not_20_out, W_Addr[3]);
  and and_1 (_0, not_1_out, not_2_out, not_3_out, not_4_out);
  and and_2 (_1, W_Addr[0], not_5_out, not_6_out, not_7_out);
  and and_3 (_2, not_8_out, W_Addr[1], not_9_out, not_10_out);
  and and_4 (_3, W_Addr[0], W_Addr[1], not_11_out, not_12_out);
  and and_5 (_4, not_13_out, not_14_out, W_Addr[2], not_15_out);
  and and_6 (_5, W_Addr[0], not_16_out, W_Addr[2], not_17_out);
  and and_7 (_6, not_18_out, W_Addr[1], W_Addr[2], not_19_out);
  and and_8 (_7, W_Addr[0], W_Addr[1], W_Addr[2], not_20_out);
endmodule

module Read_Decoder (
  input  [3:0] R_Addr,
  output _0,
  output _1,
  output _2,
  output _3,
  output _4,
  output _5,
  output _6,
  output _7
);

  wire not_1_out, not_2_out, not_3_out, not_4_out, not_5_out, not_6_out, not_7_out, not_8_out, not_9_out,
       not_10_out, not_11_out, not_12_out, not_13_out, not_14_out, not_15_out, not_16_out, not_17_out,
       not_18_out, not_19_out, not_20_out;

  not not_1 (not_1_out, R_Addr[0]);
  not not_2 (not_2_out, R_Addr[1]);
  not not_3 (not_3_out, R_Addr[2]);
  not not_4 (not_4_out, R_Addr[3]);
  not not_5 (not_5_out, R_Addr[1]);
  not not_6 (not_6_out, R_Addr[2]);
  not not_7 (not_7_out, R_Addr[3]);
  not not_8 (not_8_out, R_Addr[0]);
  not not_9 (not_9_out, R_Addr[2]);
  not not_10 (not_10_out, R_Addr[3]);
  not not_11 (not_11_out, R_Addr[2]);
  not not_12 (not_12_out, R_Addr[3]);
  not not_13 (not_13_out, R_Addr[0]);
  not not_14 (not_14_out, R_Addr[1]);
  not not_15 (not_15_out, R_Addr[3]);
  not not_16 (not_16_out, R_Addr[1]);
  not not_17 (not_17_out, R_Addr[3]);
  not not_18 (not_18_out, R_Addr[0]);
  not not_19 (not_19_out, R_Addr[3]);
  not not_20 (not_20_out, R_Addr[3]);
  and and_1 (_0, not_1_out, not_2_out, not_3_out, not_4_out);
  and and_2 (_1, R_Addr[0], not_5_out, not_6_out, not_7_out);
  and and_3 (_2, not_8_out, R_Addr[1], not_9_out, not_10_out);
  and and_4 (_3, R_Addr[0], R_Addr[1], not_11_out, not_12_out);
  and and_5 (_4, not_13_out, not_14_out, R_Addr[2], not_15_out);
  and and_6 (_5, R_Addr[0], not_16_out, R_Addr[2], not_17_out);
  and and_7 (_6, not_18_out, R_Addr[1], R_Addr[2], not_19_out);
  and and_8 (_7, R_Addr[0], R_Addr[1], R_Addr[2], not_20_out);
endmodule

module dstE (
  input  [3:0] icode,
  input  [3:0] rB,
  output [3:0] out_3
);

  wire irmovl_imm__rA_0000_out, ld_rA___addr__0010_out, or_1_out, rrmovl_rA__rB_0001_out;

  and irmovl_imm__rA_0000 (irmovl_imm__rA_0000_out, ~icode[0], ~icode[1], ~icode[2], ~icode[3]);  // AND_Gate
  and ld_rA___addr__0010 (ld_rA___addr__0010_out, ~icode[0], ~icode[1], icode[2], ~icode[3]);  // AND_Gate
  and rrmovl_rA__rB_0001 (rrmovl_rA__rB_0001_out, icode[0], ~icode[1], ~icode[2], ~icode[3]);  // AND_Gate
  or or_1 (or_1_out, irmovl_imm__rA_0000_out, ld_rA___addr__0010_out, rrmovl_rA__rB_0001_out);
  Multiplexer #(.width(4)) multiplexer_1 (.in0(4'b1111), .in1(rB), .out(out_3), .sel(or_1_out));  // open: en

  // Notes on the sheet:
  //   will output f(1111) as the base case
  //   will output rA if icode is 
  //   irmovl imm, rA 0000
  //   ld rA, <addr> 0010
endmodule

module dstM (
  input  [3:0] icode,
  input  [3:0] rB,
  output [3:0] out_3
);

  wire ld_rA___addr__0010_out, or_1_out, rrmovl_rA__rB_0001_out;

  and rrmovl_rA__rB_0001 (rrmovl_rA__rB_0001_out, icode[0], ~icode[1], ~icode[2], ~icode[3]);  // AND_Gate
  and ld_rA___addr__0010 (ld_rA___addr__0010_out, ~icode[0], icode[1], ~icode[2], ~icode[3]);  // AND_Gate
  buf or_1 (or_1_out, ld_rA___addr__0010_out);  // OR_Gate
  Multiplexer #(.width(4)) multiplexer_1 (.in0(4'b1111), .in1(rB), .out(out_3), .sel(or_1_out));  // open: en

  // Notes on the sheet:
  //   will output f(1111) as the base case
  //   will output rA if icode is 
  //   irmovl imm, rA 0000
  //   ld rA, <addr> 0010
endmodule

module srcA (
  input  [3:0] icode,
  input  [3:0] rA,
  output [3:0] out_3
);

  wire OPL_out, or_1_out, rmmovl_rA__D_rB__0011_out, rrmovl_rA__D_rB__0001_out;

  and rrmovl_rA__D_rB__0001 (rrmovl_rA__D_rB__0001_out, icode[0], ~icode[1], ~icode[2], ~icode[3]);  // AND_Gate
  and rmmovl_rA__D_rB__0011 (rmmovl_rA__D_rB__0011_out, icode[0], icode[1], ~icode[2], ~icode[3]);  // AND_Gate
  and OPL (OPL_out, ~icode[0], ~icode[1], icode[2], ~icode[3]);  // AND_Gate
  or or_1 (or_1_out, rrmovl_rA__D_rB__0001_out, rmmovl_rA__D_rB__0011_out, OPL_out);
  Multiplexer #(.width(4)) multiplexer_1 (.in0(4'b1111), .in1(rA), .out(out_3), .sel(or_1_out));  // open: en

  // Notes on the sheet:
  //   will output f(1111) as the base case
  //   will output rA if icode is 
  //   rrmovl rA, D(rB) 0001
  //   rmmovl rA, D(rB) 0011
  //   OPL rA, rB 0100
endmodule

module srcB (
  input  [3:0] icode,
  input  [3:0] rB,
  output [3:0] out_3
);

  wire mrmovl_out, OPL_out, or_1_out, rrmovl_rA__D_rB__0001_out;

  and rrmovl_rA__D_rB__0001 (rrmovl_rA__D_rB__0001_out, icode[0], ~icode[1], ~icode[2], ~icode[3]);  // AND_Gate
  and mrmovl (mrmovl_out, ~icode[0], icode[1], ~icode[2], ~icode[3]);  // AND_Gate
  and OPL (OPL_out, ~icode[0], ~icode[1], icode[2], ~icode[3]);  // AND_Gate
  buf or_1 (or_1_out, OPL_out);  // OR_Gate
  Multiplexer #(.width(4)) multiplexer_1 (.in0(4'b1111), .in1(rB), .out(out_3), .sel(or_1_out));  // open: en

  // Notes on the sheet:
  //   will output f(1111) as the base case
  //   will output rB if icode is 
  //   rrmovl rA, D(rB) 0001
  //   mrmovl D(rB), rA 0010
  //   OPL rA, rB 0100
endmodule

module Register_Helper (
  input  [31:0] DataM,
  input  [31:0] DataE,
  input  Select_M,
  input  Select_E,
  output [31:0] Data,
  output Select
);

  or or_1 (Select, Select_M, Select_E);
  Multiplexer #(.width(32)) multiplexer_1 (.in0(DataM), .in1(DataE), .out(Data), .sel(Select_E));  // open: en
endmodule
