// Logisim project Fetch.circ as structural Verilog: 7 circuits, main circuit main
module main (
  output [3:0] iCode,
  output [3:0] ifun,
  output [3:0] rA,
  output [15:0] valP,
  output [3:0] rB,
  output [31:0] valC,
  output [15:0] out_7,
  output [15:0] out_8
);

  wire clock_1_out, fetch_unit_1_need_rgs, fetch_unit_1_need_valc;

  Clock clock_1 (.out(clock_1_out));
  Fetch_Unit fetch_unit_1 (
    .Address_PC(out_7), .icode(iCode), .ifun(ifun), .rA(rA), .rB(rB), .valC(valC),
    .need_Rgs(fetch_unit_1_need_rgs), .need_valC(fetch_unit_1_need_valc), .Clock(clock_1_out));
  PC pc_1 (.Clock(clock_1_out), .in(out_8), .out(out_7));
  newNewPC newnewpc_1 (
    .iCode(iCode), .Clock(clock_1_out), .valC(valC), .new_PC(out_8), .valP(valP));  // open: Cnd, valM
  PC_Increment pc_increment_1 (
    .valP(valP), .in_3(out_7), .needValC(fetch_unit_1_need_valc), .need_regId(fetch_unit_1_need_rgs));
endmodule

// New PC
module New_Pc (
  input  [3:0] iCode,
  input  Clock,
  input  [31:0] valC,
  input  [15:0] valP,
  output [15:0] out
);


  assign out = valP;
endmodule

module PC_Increment (
  input  needValC,
  input  need_regId,
  input  [15:0] in_3,
  output [15:0] valP
);

  wire [2:2] or_1_out;
  wire [15:0] adder_1_out, adder_2_out;

  Adder #(.width(16)) adder_1 (.a(in_3), .b(16'h1), .out(adder_1_out));  // open: cin, cout
  or or_1 (or_1_out[2], needValC, need_regId, 1'b1);
  Adder #(.width(16)) adder_2 (.a(adder_1_out), .b({{15{1'b0}}, or_1_out[2]}), .out(adder_2_out));  // open: cin, cout
  Adder #(.width(16)) adder_3 (.a({{13{1'b0}}, or_1_out[2], 2'b00}), .b(adder_2_out), .out(valP));  // open: cin, cout
endmodule

module Fetch_Unit (
  input  Clock,
  input  [15:0] Address_PC,
  output [3:0] rA,
  output [3:0] icode,
  output [31:0] valC,
  output need_Rgs,
  output [3:0] ifun,
  output [3:0] rB,
  output need_valC
);

  wire decoder_1_out7, decoder_2_out0, decoder_2_out1, decoder_2_out2, decoder_2_out3, decoder_2_out4,
       decoder_3_out0, decoder_3_out1, decoder_3_out2, decoder_3_out3, decoder_3_out5, n3bitencoder_1_out_4,
       n3bitencoder_1_out_5, n3bitencoder_1_out_6, n3bitencoder_1_out_7, n3bitencoder_1_out_8,
       n3bitencoder_1_out_9;
  wire [2:0] counter_2_q;
  wire [7:0] rom_1_data;
  wire [15:0] adder_1_out, counter_1_q, multiplexer_1_out;

  Decoder #(.select(4)) decoder_1 (
    .out7(decoder_1_out7), .sel(icode));  // open: out0, out1, out2, out3, out4, out5, out6, out8, out9, out10, out11, out12, out13, out14, out15, en
  Register register_1 (.D(rom_1_data), .en(n3bitencoder_1_out_4), .Q({icode, ifun}), .clk(Clock));  // open: clr
  Multiplexer #(.width(16)) multiplexer_1 (
    .in0(counter_1_q), .in1({16{1'b0}}), .out(multiplexer_1_out), .sel(decoder_1_out7));  // open: en
  Register register_2 (.D(rom_1_data), .en(n3bitencoder_1_out_5), .Q({rA, rB}), .clk(Clock));  // open: clr
  _3BitEncoder u_3bitencoder_1 (
    ._0(counter_2_q[0]), ._1(counter_2_q[1]), ._2(counter_2_q[2]), .out_4(n3bitencoder_1_out_4),
    .out_5(n3bitencoder_1_out_5), .out_8(n3bitencoder_1_out_8), .out_6(n3bitencoder_1_out_6),
    .out_7(n3bitencoder_1_out_7), .out_9(n3bitencoder_1_out_9));
  Counter #(.width(16), .max('h5)) counter_1 (.count(1'b1), .Q(counter_1_q), .clk(Clock));  // open: load, D, carry, clr
  Adder #(.width(16)) adder_1 (.a(Address_PC), .b(multiplexer_1_out), .out(adder_1_out));  // open: cin, cout
  Register register_3 (.D(rom_1_data), .en(n3bitencoder_1_out_9), .Q(valC[31:24]), .clk(Clock));  // open: clr
  Register register_4 (.D(rom_1_data), .en(n3bitencoder_1_out_7), .Q(valC[23:16]), .clk(Clock));  // open: clr
  Counter #(.width(3), .max('h5)) counter_2 (.count(1'b1), .Q(counter_2_q), .clk(Clock));  // open: load, D, carry, clr
  Register register_5 (.D(rom_1_data), .en(n3bitencoder_1_out_6), .Q(valC[15:8]), .clk(Clock));  // open: clr
  ROM #(.addrWidth(16)) rom_1 (.addr(adder_1_out), .data(rom_1_data));  // open: sel
  Register register_6 (.D(rom_1_data), .en(n3bitencoder_1_out_8), .Q(valC[7:0]), .clk(Clock));  // open: clr
  Decoder #(.select(4)) decoder_2 (
    .out0(decoder_2_out0), .out1(decoder_2_out1), .out2(decoder_2_out2), .out3(decoder_2_out3),
    .out4(decoder_2_out4), .sel(icode), .en(1'b1));  // open: out5, out6, out7, out8, out9, out10, out11, out12, out13, out14, out15
  Decoder #(.select(4)) decoder_3 (
    .out0(decoder_3_out0), .out1(decoder_3_out1), .out2(decoder_3_out2), .out3(decoder_3_out3),
    .out5(decoder_3_out5), .sel(icode), .en(1'b1));  // open: out4, out6, out7, out8, out9, out10, out11, out12, out13, out14, out15
  or or_1 (need_Rgs, decoder_2_out2, decoder_2_out3, decoder_2_out4, decoder_2_out1, decoder_2_out0);
  or or_2 (need_valC, decoder_3_out0, decoder_3_out1, decoder_3_out5, decoder_3_out3, decoder_3_out2);

  // Notes on the sheet:
  //   contents of rom_1 (hex, n*v repeats v):
  //   0 f0 3 4*0 f1 2 4*0 f2 6 4*0 f3 1 0 0 0 30 5*0 30 10 1 0 0 0 30 20 2 0 0 0 30 30 3 4*0 f4 4 4*0 f5 6
  //   4*0 f6 3 4*0 f7 9 0 0 0 30 40 4 0 0 0 30 50 5 0 0 0 30 60 6 0 0 0 30 70 7 0 0 0 20 40 4*0 20 50 1 0
  //   0 0 20 60 2 0 0 0 20 70 3 0 0 0 20 0 4 0 0 0 20 10 5 0 0 0 20 20 6 0 0 0 20 30 7 0 0 0 40 4 4*0 40
  //   15 4*0 40 26 4*0 40 37 4*0 30 40 8 0 0 0 30 50 9 0 0 0 30 60 a 0 0 0 30 70 b 0 0 0 70
endmodule

module PC (
  input  [15:0] in,
  input  Clock,
  output [15:0] out
);

  wire decoder_1_out5;
  wire [2:0] counter_1_q;
  wire [15:0] multiplexer_1_out;

  Multiplexer #(.width(16)) multiplexer_1 (
    .in1(in), .out(multiplexer_1_out), .sel(decoder_1_out5), .en(1'b1));  // open: in0
  Counter #(.width(3), .max('h5)) counter_1 (.count(1'b1), .Q(counter_1_q), .clk(Clock));  // open: load, D, carry, clr
  Decoder #(.select(3)) decoder_1 (
    .out5(decoder_1_out5), .sel(counter_1_q), .en(1'b1));  // open: out0, out1, out2, out3, out4, out6, out7
  Register #(.width(16)) register_1 (.D(multiplexer_1_out), .Q(out), .clk(Clock));  // open: en, clr
endmodule

module _3BitEncoder (
  input  _0,
  input  _1,
  input  _2,
  output out_4,
  output out_5,
  output out_6,
  output out_7,
  output out_8,
  output out_9
);

  wire not_1_out, not_2_out, not_3_out;

  not not_1 (not_1_out, _0);
  not not_2 (not_2_out, _1);
  not not_3 (not_3_out, _2);
  and _000 (out_4, not_3_out, not_2_out, not_1_out);
  and _001 (out_5, not_3_out, not_2_out, _0);
  and _010 (out_8, not_3_out, _1, not_1_out);
  and _011 (out_6, not_3_out, _1, _0);
  and _100 (out_7, _2, not_2_out, not_1_out);
  and _101 (out_9, _0, not_2_out, _2);
endmodule

module newNewPC (
  input  [3:0] iCode,
  input  Clock,
  input  Cnd,
  input  [15:0] valP,
  input  [31:0] valM,
  input  [31:0] valC,
  output [15:0] new_PC
);

  wire decoder_1_out7, not_1_out;
  wire [15:0] multiplexer_1_out;

  // OR_Gate or_1 is placed but not wired
  Decoder #(.select(4)) decoder_1 (
    .out7(decoder_1_out7), .sel(iCode));  // open: out0, out1, out2, out3, out4, out5, out6, out8, out9, out10, out11, out12, out13, out14, out15, en
  Multiplexer #(.width(16)) multiplexer_1 (
    .in0(valC[15:0]), .in1(valP), .out(multiplexer_1_out), .sel(Cnd));  // open: en
  not not_1 (not_1_out, decoder_1_out7);
  Multiplexer #(.select(4), .width(16)) multiplexer_2 (
    .in0(valP), .in1(valP), .in2(valP), .in3(valP), .in4(valP), .in5(multiplexer_1_out),
    .in6(multiplexer_1_out), .in7(valP), .in8(valC[15:0]), .in9(valP), .in10(valP), .in11(valP), .in12(valP),
    .in13(valP), .in14(valP), .in15(valP), .out(new_PC), .sel(iCode), .en(not_1_out));
endmodule
