// Logisim project Execute.circ as structural Verilog: 15 circuits, main circuit main
module main (
  input  Clock,
  input  [3:0] icode,
  input  [3:0] ifun,
  input  [31:0] ValC,
  input  [31:0] ValA,
  input  [31:0] ValB,
  output [31:0] out_7
);

  wire cond_1_condflag, set_cc_1_cc;
  wire [2:0] alu_1_out_6, cc_1_out_3;
  wire [3:0] alu_fun_1_out_3;
  wire [31:0] alua_1_out_4, alub_1_out_3;

  Cond cond_1 (.ifun(ifun), .CC(cc_1_out_3), .condFlag(cond_1_condflag));
  CC cc_1 (.CC(alu_1_out_6), .setCC(set_cc_1_cc), .out_3(cc_1_out_3));
  set_CC set_cc_1 (.CC(set_cc_1_cc), .icode(icode));
  ALUA alua_1 (.out_4(alua_1_out_4), .icode(icode), .ValC(ValC), .ValA(ValA));
  ALU alu_1 (
    .ALU_fun(alu_fun_1_out_3), .ALUA(alua_1_out_4), .ALUB(alub_1_out_3), .ValE(out_7), .Clock(Clock),
    .out_6(alu_1_out_6));
  ALUB alub_1 (.out_3(alub_1_out_3), .icode(icode), .ValB(ValB));
  ALU_fun alu_fun_1 (.out_3(alu_fun_1_out_3), .icode(icode), .ifun(ifun));

  // Notes on the sheet:
  //   Bit 0: overflow
  //   Bit 1: Negative
  //   Bit 2: Zero
  //   0000 = Add
  //   0001 = Multiply
  //   0010 = Subtract
  //   0011 = AND
  //   0100 = OR
  //   icode
  //   0100 = OPL
  //   0101 = jmp
  //   0110 = jxx
endmodule

module ALU (
  input  [31:0] ALUA,
  input  [31:0] ALUB,
  input  [3:0] ALU_fun,
  input  Clock,
  output [31:0] ValE,
  output [2:0] out_6
);

  wire n32_bit_adder_1_overflow, n32_bit_subtractor_1_negative_flag, undriven;
  wire [2:0] alu_helper_1_cc;
  wire [7:0] counter_1_q;
  wire [31:0] alu_helper_1_output, and_2_out, multiplier_1_cout, multiplier_1_out, n32_bit_adder_1_out_4,
       n32_bit_subtractor_1_out_4, or_1_out;

  Counter #(.max('h5)) counter_1 (.Q(counter_1_q), .clk(undriven));  // open: load, D, count, carry, clr
  _32_bit_Adder u_32_bit_adder_1 (
    .A(ALUA), .B(ALUB), .out_4(n32_bit_adder_1_out_4), .Overflow(n32_bit_adder_1_overflow));
  // AND_Gate and_1 has open pins: in0=counter_1_q[0], in1=counter_1_q[1], in2=counter_1_q[2], in3=counter_1_q[3], in4=counter_1_q[4], out=open
  Multiplier #(.width(32)) multiplier_1 (
    .a(ALUB), .b(ALUA), .out(multiplier_1_out), .cout(multiplier_1_cout));  // open: cin
  ALU_Helper alu_helper_1 (
    .ifun(ALU_fun), .Output(alu_helper_1_output), .CC(alu_helper_1_cc), .Mult_overflow(multiplier_1_cout),
    .Adder_Overflow(n32_bit_adder_1_overflow), .Add(n32_bit_adder_1_out_4), .Mult(multiplier_1_out),
    .Sub(n32_bit_subtractor_1_out_4), .Subtractor_Negative(n32_bit_subtractor_1_negative_flag),
    .And(and_2_out), .Or(or_1_out));
  Register #(.width(3)) register_1 (.D(alu_helper_1_cc), .Q(out_6), .clk(Clock));  // open: en, clr
  _32_bit_Subtractor u_32_bit_subtractor_1 (
    .A(ALUA), .B(ALUB), .out_4(n32_bit_subtractor_1_out_4), .Negative_flag(n32_bit_subtractor_1_negative_flag));
  Register #(.width(32)) register_2 (.D(alu_helper_1_output), .Q(ValE), .clk(Clock));  // open: en, clr
  assign and_2_out = ALUA & ALUB;  // AND_Gate and_2, 32 bits wide
  assign or_1_out = ALUA | ALUB;  // OR_Gate or_1, 32 bits wide

  // Notes on the sheet:
  //   0000 = Add
  //   0001 = Multiply
  //   0010 = Subtract
  //   0011 = AND
  //   0100 = OR
  //   0010
  //   Bit 0: overflow
  //   Bit 1: Negative
  //   Bit 2: Zero
  //   0011
  //   0100
  //   0101
endmodule

module ALU_Helper (
  input  [31:0] Add,
  input  [31:0] Mult,
  input  [31:0] Sub,
  input  [31:0] And,
  input  [31:0] Or,
  input  [31:0] Mult_overflow,
  input  [3:0] ifun,
  input  Subtractor_Negative,
  input  Adder_Overflow,
  output [31:0] Output,
  output [2:0] CC
);

  wire n32_bit_magnitude_comparator_1_e, not_1_out;

  _32_bit_Magnitude_Comparator u_32_bit_magnitude_comparator_1 (
    .A({32{1'b0}}), .B(Mult_overflow), .e(n32_bit_magnitude_comparator_1_e));  // open: gt, lt
  not not_1 (not_1_out, n32_bit_magnitude_comparator_1_e);
  Multiplexer multiplexer_1 (.in0(Adder_Overflow), .in1(not_1_out), .out(CC[0]), .sel(ifun[0]));  // open: en
  and and_1 (CC[1], ~ifun[0], ifun[1], Subtractor_Negative);  // AND_Gate
  Multiplexer #(.select(3), .width(32)) multiplexer_2 (
    .in0(Add), .in1(Mult), .in2(Sub), .in3(And), .in4(Or), .in5({32{1'b0}}), .in6({32{1'b0}}),
    .in7({32{1'b0}}), .out(Output), .sel(ifun[2:0]));  // open: en
  _32_bit_Magnitude_Comparator u_32_bit_magnitude_comparator_2 (.A(Output), .B({32{1'b0}}), .e(CC[2]));  // open: gt, lt

  // Notes on the sheet:
  //   Bit 0: overflow
  //   Bit 1: Negative
  //   Bit 2: Zero
endmodule

module ALUA (
  input  [31:0] ValC,
  input  [31:0] ValA,
  input  [3:0] icode,
  output [31:0] out_4
);

  wire and_1_out, and_2_out, and_3_out, or_1_out;

  and and_1 (and_1_out, ~icode[3], ~icode[2], ~icode[1], icode[0]);  // AND_Gate
  or or_1 (or_1_out, and_1_out, and_2_out);
  and and_2 (and_2_out, ~icode[3], icode[2], ~icode[1], ~icode[0]);  // AND_Gate
  and and_3 (and_3_out, ~icode[3], ~icode[2], icode[1], icode[0]);  // AND_Gate
  Multiplexer #(.width(32)) multiplexer_1 (.in0(ValC), .in1(ValA), .out(out_4), .sel(or_1_out));  // open: en

  // Notes on the sheet:
  //   0001 -- rrmov rA, D(rB)
  //   0100 -- OPL rA, rB
  //   If icode is 0100 or 0001, valA will out put, else, ValC will output
  //   on selects valA
endmodule

module ALUB (
  input  [31:0] ValB,
  input  [3:0] icode,
  output [31:0] out_3
);

  wire and_1_out, and_2_out, or_1_out;

  and and_1 (and_1_out, ~icode[3], ~icode[2], icode[1], ~icode[0]);  // AND_Gate
  buf or_1 (or_1_out, and_2_out);  // OR_Gate
  and and_2 (and_2_out, ~icode[3], icode[2], ~icode[1], ~icode[0]);  // AND_Gate
  Multiplexer #(.width(32)) multiplexer_1 (.in0({32{1'b0}}), .in1(ValB), .out(out_3), .sel(or_1_out));  // open: en

  // Notes on the sheet:
  //   0010 - ld rA, <addr>
  //   0011 - st rA, <addr>
  //   0100 - OPL ra, rB
  //   on selects valA
endmodule

module ALU_fun (
  input  [3:0] ifun,
  input  [3:0] icode,
  output [3:0] out_3
);

  wire _0100_out, _0101_out, _0110_out, or_1_out;

  and _0100 (_0100_out, ~icode[3], icode[2], ~icode[1], ~icode[0]);  // AND_Gate
  or or_1 (or_1_out, _0100_out, _0101_out, _0110_out);
  and _0101 (_0101_out, ~icode[3], icode[2], ~icode[1], icode[0]);  // AND_Gate
  and _0110 (_0110_out, ~icode[3], icode[2], icode[1], ~icode[0]);  // AND_Gate
  Multiplexer #(.width(4)) multiplexer_1 (.in0(4'b0000), .in1(ifun), .out(out_3), .sel(or_1_out));  // open: en

  // Notes on the sheet:
  //   OPL
  //   jmp
  //   jmp cond
endmodule

module CC (
  input  [2:0] CC,
  input  setCC,
  output [2:0] out_3
);

  Multiplexer #(.width(3)) multiplexer_1 (.in0(3'b000), .in1(CC), .out(out_3), .sel(setCC));  // open: en
endmodule

module set_CC (
  input  [3:0] icode,
  output CC
);

  and _0100 (CC, ~icode[3], icode[2], ~icode[1], ~icode[0]);  // AND_Gate

  // Notes on the sheet:
  //   OPL
  //   If icode is OPL output 1, else output 0 as condition code set bit
endmodule

// Adder
module _32_bit_Adder (
  input  [31:0] A,
  input  [31:0] B,
  output Overflow,
  output [31:0] out_4
);

  wire full_adder_2_co, full_adder_3_co, full_adder_4_co, full_adder_5_co, full_adder_6_co, full_adder_7_co,
       full_adder_8_co, full_adder_9_co, full_adder_10_co, full_adder_11_co, full_adder_12_co,
       full_adder_13_co, full_adder_14_co, full_adder_15_co, full_adder_16_co, full_adder_17_co,
       full_adder_18_co, full_adder_19_co, full_adder_20_co, full_adder_21_co, full_adder_22_co,
       full_adder_23_co, full_adder_24_co, full_adder_25_co, full_adder_26_co, full_adder_27_co,
       full_adder_28_co, full_adder_29_co, full_adder_30_co, full_adder_31_co, half_adder_1_co;

  Full_Adder full_adder_1 (.A(A[31]), .B(B[31]), .ci(full_adder_2_co), .sum(out_4[31]), .co(Overflow));
  Full_Adder full_adder_2 (.A(A[30]), .B(B[30]), .ci(full_adder_3_co), .sum(out_4[30]), .co(full_adder_2_co));
  Full_Adder full_adder_3 (.A(A[29]), .B(B[29]), .ci(full_adder_5_co), .sum(out_4[29]), .co(full_adder_3_co));
  Full_Adder full_adder_4 (.A(A[27]), .B(B[27]), .ci(full_adder_7_co), .sum(out_4[27]), .co(full_adder_4_co));
  Full_Adder full_adder_5 (.A(A[28]), .B(B[28]), .ci(full_adder_4_co), .sum(out_4[28]), .co(full_adder_5_co));
  Full_Adder full_adder_6 (.A(A[24]), .B(B[24]), .ci(full_adder_11_co), .sum(out_4[24]), .co(full_adder_6_co));
  Full_Adder full_adder_7 (.A(A[26]), .B(B[26]), .ci(full_adder_8_co), .sum(out_4[26]), .co(full_adder_7_co));
  Full_Adder full_adder_8 (.A(A[25]), .B(B[25]), .ci(full_adder_6_co), .sum(out_4[25]), .co(full_adder_8_co));
  Full_Adder full_adder_9 (.A(A[22]), .B(B[22]), .ci(full_adder_10_co), .sum(out_4[22]), .co(full_adder_9_co));
  Full_Adder full_adder_10 (.A(A[21]), .B(B[21]), .ci(full_adder_12_co), .sum(out_4[21]), .co(full_adder_10_co));
  Full_Adder full_adder_11 (.A(A[23]), .B(B[23]), .ci(full_adder_9_co), .sum(out_4[23]), .co(full_adder_11_co));
  Full_Adder full_adder_12 (.A(A[20]), .B(B[20]), .ci(full_adder_13_co), .sum(out_4[20]), .co(full_adder_12_co));
  Full_Adder full_adder_13 (.A(A[19]), .B(B[19]), .ci(full_adder_16_co), .sum(out_4[19]), .co(full_adder_13_co));
  Full_Adder full_adder_14 (.A(A[16]), .B(B[16]), .ci(full_adder_18_co), .sum(out_4[16]), .co(full_adder_14_co));
  Full_Adder full_adder_15 (.A(A[17]), .B(B[17]), .ci(full_adder_14_co), .sum(out_4[17]), .co(full_adder_15_co));
  Full_Adder full_adder_16 (.A(A[18]), .B(B[18]), .ci(full_adder_15_co), .sum(out_4[18]), .co(full_adder_16_co));
  Full_Adder full_adder_17 (.A(A[14]), .B(B[14]), .ci(full_adder_19_co), .sum(out_4[14]), .co(full_adder_17_co));
  Full_Adder full_adder_18 (.A(A[15]), .B(B[15]), .ci(full_adder_17_co), .sum(out_4[15]), .co(full_adder_18_co));
  Full_Adder full_adder_19 (.A(A[13]), .B(B[13]), .ci(full_adder_20_co), .sum(out_4[13]), .co(full_adder_19_co));
  Full_Adder full_adder_20 (.A(A[12]), .B(B[12]), .ci(full_adder_21_co), .sum(out_4[12]), .co(full_adder_20_co));
  Full_Adder full_adder_21 (.A(A[11]), .B(B[11]), .ci(full_adder_23_co), .sum(out_4[11]), .co(full_adder_21_co));
  Full_Adder full_adder_22 (.A(A[8]), .B(B[8]), .ci(full_adder_27_co), .sum(out_4[8]), .co(full_adder_22_co));
  Full_Adder full_adder_23 (.A(A[10]), .B(B[10]), .ci(full_adder_24_co), .sum(out_4[10]), .co(full_adder_23_co));
  Full_Adder full_adder_24 (.A(A[9]), .B(B[9]), .ci(full_adder_22_co), .sum(out_4[9]), .co(full_adder_24_co));
  Full_Adder full_adder_25 (.A(A[5]), .B(B[5]), .ci(full_adder_29_co), .sum(out_4[5]), .co(full_adder_25_co));
  Full_Adder full_adder_26 (.A(A[6]), .B(B[6]), .ci(full_adder_25_co), .sum(out_4[6]), .co(full_adder_26_co));
  Full_Adder full_adder_27 (.A(A[7]), .B(B[7]), .ci(full_adder_26_co), .sum(out_4[7]), .co(full_adder_27_co));
  Full_Adder full_adder_28 (.A(A[3]), .B(B[3]), .ci(full_adder_30_co), .sum(out_4[3]), .co(full_adder_28_co));
  Full_Adder full_adder_29 (.A(A[4]), .B(B[4]), .ci(full_adder_28_co), .sum(out_4[4]), .co(full_adder_29_co));
  Full_Adder full_adder_30 (.A(A[2]), .B(B[2]), .ci(full_adder_31_co), .sum(out_4[2]), .co(full_adder_30_co));
  Full_Adder full_adder_31 (.A(A[1]), .B(B[1]), .ci(half_adder_1_co), .sum(out_4[1]), .co(full_adder_31_co));
  Half_Adder half_adder_1 (.A(A[0]), .B(B[0]), .co(half_adder_1_co), .sum(out_4[0]));
endmodule

module Full_Adder (
  input  A,
  input  B,
  input  ci,
  output sum,
  output co
);

  wire and_1_out, and_2_out, xor_1_out;

  xor xor_1 (xor_1_out, A, B);
  xor xor_2 (sum, xor_1_out, ci);
  and and_1 (and_1_out, ci, xor_1_out);
  and and_2 (and_2_out, A, B);
  or or_1 (co, and_1_out, and_2_out);
endmodule

module Half_Adder (
  input  A,
  input  B,
  output co,
  output sum
);

  and and_1 (co, A, B);
  xor xor_1 (sum, A, B);
endmodule

// Subtractor
module _32_bit_Subtractor (
  input  [31:0] B,
  input  [31:0] A,
  output Negative_flag,
  output [31:0] out_4
);

  wire [31:0] n32_bit_adder_1_out_4, not_1_out;

  assign not_1_out = ~B;  // NOT_Gate not_1, 32 bits wide
  _32_bit_Adder u_32_bit_adder_1 (.A(not_1_out), .B(32'h1), .out_4(n32_bit_adder_1_out_4));  // open: Overflow
  _32_bit_Adder u_32_bit_adder_2 (.A(A), .B(n32_bit_adder_1_out_4), .out_4(out_4));  // open: Overflow
  _32_bit_Magnitude_Comparator u_32_bit_magnitude_comparator_1 (.A(B), .B(A), .gt(Negative_flag));  // open: e, lt
endmodule

module _32_bit_Magnitude_Comparator (
  input  [31:0] A,
  input  [31:0] B,
  output gt,
  output e,
  output lt
);

  wire n1_bit_mc_1_out_eq, n1_bit_mc_1_out_gt, n1_bit_mc_1_out_lt, n1_bit_mc_2_out_eq, n1_bit_mc_2_out_gt,
       n1_bit_mc_2_out_lt, n1_bit_mc_3_out_eq, n1_bit_mc_3_out_gt, n1_bit_mc_3_out_lt, n1_bit_mc_4_out_eq,
       n1_bit_mc_4_out_gt, n1_bit_mc_4_out_lt, n1_bit_mc_5_out_eq, n1_bit_mc_5_out_gt, n1_bit_mc_5_out_lt,
       n1_bit_mc_6_out_eq, n1_bit_mc_6_out_gt, n1_bit_mc_6_out_lt, n1_bit_mc_7_out_eq, n1_bit_mc_7_out_gt,
       n1_bit_mc_7_out_lt, n1_bit_mc_8_out_eq, n1_bit_mc_8_out_gt, n1_bit_mc_8_out_lt, n1_bit_mc_9_out_eq,
       n1_bit_mc_9_out_gt, n1_bit_mc_9_out_lt, n1_bit_mc_10_out_eq, n1_bit_mc_10_out_gt, n1_bit_mc_10_out_lt,
       n1_bit_mc_11_out_eq, n1_bit_mc_11_out_gt, n1_bit_mc_11_out_lt, n1_bit_mc_12_out_eq,
       n1_bit_mc_12_out_gt, n1_bit_mc_12_out_lt, n1_bit_mc_13_out_eq, n1_bit_mc_13_out_gt,
       n1_bit_mc_13_out_lt, n1_bit_mc_14_out_eq, n1_bit_mc_14_out_gt, n1_bit_mc_14_out_lt,
       n1_bit_mc_15_out_eq, n1_bit_mc_15_out_gt, n1_bit_mc_15_out_lt, n1_bit_mc_16_out_eq,
       n1_bit_mc_16_out_gt, n1_bit_mc_16_out_lt, n1_bit_mc_17_out_eq, n1_bit_mc_17_out_gt,
       n1_bit_mc_17_out_lt, n1_bit_mc_18_out_eq, n1_bit_mc_18_out_gt, n1_bit_mc_18_out_lt,
       n1_bit_mc_19_out_eq, n1_bit_mc_19_out_gt, n1_bit_mc_19_out_lt, n1_bit_mc_20_out_eq,
       n1_bit_mc_20_out_gt, n1_bit_mc_20_out_lt, n1_bit_mc_21_out_eq, n1_bit_mc_21_out_gt,
       n1_bit_mc_21_out_lt, n1_bit_mc_22_out_eq, n1_bit_mc_22_out_gt, n1_bit_mc_22_out_lt,
       n1_bit_mc_23_out_eq, n1_bit_mc_23_out_gt, n1_bit_mc_23_out_lt, n1_bit_mc_24_out_eq,
       n1_bit_mc_24_out_gt, n1_bit_mc_24_out_lt, n1_bit_mc_25_out_eq, n1_bit_mc_25_out_gt,
       n1_bit_mc_25_out_lt, n1_bit_mc_26_out_eq, n1_bit_mc_26_out_gt, n1_bit_mc_26_out_lt,
       n1_bit_mc_27_out_eq, n1_bit_mc_27_out_gt, n1_bit_mc_27_out_lt, n1_bit_mc_28_out_eq,
       n1_bit_mc_28_out_gt, n1_bit_mc_28_out_lt, n1_bit_mc_29_out_eq, n1_bit_mc_29_out_gt,
       n1_bit_mc_29_out_lt, n1_bit_mc_30_out_eq, n1_bit_mc_30_out_gt, n1_bit_mc_30_out_lt,
       n1_bit_mc_31_out_eq, n1_bit_mc_31_out_gt, n1_bit_mc_31_out_lt;

  _1_bit_MC u_1_bit_mc_1 (
    .in_gt(n1_bit_mc_3_out_gt), .in_eq(n1_bit_mc_3_out_eq), .in_lt(n1_bit_mc_3_out_lt),
    .out_gt(n1_bit_mc_1_out_gt), .out_eq(n1_bit_mc_1_out_eq), .out_lt(n1_bit_mc_1_out_lt), .A(A[29]),
    .B(B[29]));
  _1_bit_MC u_1_bit_mc_2 (
    .in_gt(1'b0), .in_eq(1'b1), .in_lt(1'b0), .out_gt(n1_bit_mc_2_out_gt), .out_eq(n1_bit_mc_2_out_eq),
    .out_lt(n1_bit_mc_2_out_lt), .A(A[31]), .B(B[31]));
  _1_bit_MC u_1_bit_mc_3 (
    .in_gt(n1_bit_mc_2_out_gt), .in_eq(n1_bit_mc_2_out_eq), .in_lt(n1_bit_mc_2_out_lt),
    .out_gt(n1_bit_mc_3_out_gt), .out_eq(n1_bit_mc_3_out_eq), .out_lt(n1_bit_mc_3_out_lt), .A(A[30]),
    .B(B[30]));
  _1_bit_MC u_1_bit_mc_4 (
    .in_gt(n1_bit_mc_1_out_gt), .in_eq(n1_bit_mc_1_out_eq), .in_lt(n1_bit_mc_1_out_lt),
    .out_gt(n1_bit_mc_4_out_gt), .out_eq(n1_bit_mc_4_out_eq), .out_lt(n1_bit_mc_4_out_lt), .A(A[28]),
    .B(B[28]));
  _1_bit_MC u_1_bit_mc_5 (
    .in_gt(n1_bit_mc_4_out_gt), .in_eq(n1_bit_mc_4_out_eq), .in_lt(n1_bit_mc_4_out_lt),
    .out_gt(n1_bit_mc_5_out_gt), .out_eq(n1_bit_mc_5_out_eq), .out_lt(n1_bit_mc_5_out_lt), .A(A[27]),
    .B(B[27]));
  _1_bit_MC u_1_bit_mc_6 (
    .in_gt(n1_bit_mc_5_out_gt), .in_eq(n1_bit_mc_5_out_eq), .in_lt(n1_bit_mc_5_out_lt),
    .out_gt(n1_bit_mc_6_out_gt), .out_eq(n1_bit_mc_6_out_eq), .out_lt(n1_bit_mc_6_out_lt), .A(A[26]),
    .B(B[26]));
  _1_bit_MC u_1_bit_mc_7 (
    .in_gt(n1_bit_mc_8_out_gt), .in_eq(n1_bit_mc_8_out_eq), .in_lt(n1_bit_mc_8_out_lt),
    .out_gt(n1_bit_mc_7_out_gt), .out_eq(n1_bit_mc_7_out_eq), .out_lt(n1_bit_mc_7_out_lt), .A(A[24]),
    .B(B[24]));
  _1_bit_MC u_1_bit_mc_8 (
    .in_gt(n1_bit_mc_6_out_gt), .in_eq(n1_bit_mc_6_out_eq), .in_lt(n1_bit_mc_6_out_lt),
    .out_gt(n1_bit_mc_8_out_gt), .out_eq(n1_bit_mc_8_out_eq), .out_lt(n1_bit_mc_8_out_lt), .A(A[25]),
    .B(B[25]));
  _1_bit_MC u_1_bit_mc_9 (
    .in_gt(n1_bit_mc_10_out_gt), .in_eq(n1_bit_mc_10_out_eq), .in_lt(n1_bit_mc_10_out_lt),
    .out_gt(n1_bit_mc_9_out_gt), .out_eq(n1_bit_mc_9_out_eq), .out_lt(n1_bit_mc_9_out_lt), .A(A[22]),
    .B(B[22]));
  _1_bit_MC u_1_bit_mc_10 (
    .in_gt(n1_bit_mc_7_out_gt), .in_eq(n1_bit_mc_7_out_eq), .in_lt(n1_bit_mc_7_out_lt),
    .out_gt(n1_bit_mc_10_out_gt), .out_eq(n1_bit_mc_10_out_eq), .out_lt(n1_bit_mc_10_out_lt), .A(A[23]),
    .B(B[23]));
  _1_bit_MC u_1_bit_mc_11 (
    .in_gt(n1_bit_mc_9_out_gt), .in_eq(n1_bit_mc_9_out_eq), .in_lt(n1_bit_mc_9_out_lt),
    .out_gt(n1_bit_mc_11_out_gt), .out_eq(n1_bit_mc_11_out_eq), .out_lt(n1_bit_mc_11_out_lt), .A(A[21]),
    .B(B[21]));
  _1_bit_MC u_1_bit_mc_12 (
    .in_gt(n1_bit_mc_13_out_gt), .in_eq(n1_bit_mc_13_out_eq), .in_lt(n1_bit_mc_13_out_lt),
    .out_gt(n1_bit_mc_12_out_gt), .out_eq(n1_bit_mc_12_out_eq), .out_lt(n1_bit_mc_12_out_lt), .A(A[18]),
    .B(B[18]));
  _1_bit_MC u_1_bit_mc_13 (
    .in_gt(n1_bit_mc_14_out_gt), .in_eq(n1_bit_mc_14_out_eq), .in_lt(n1_bit_mc_14_out_lt),
    .out_gt(n1_bit_mc_13_out_gt), .out_eq(n1_bit_mc_13_out_eq), .out_lt(n1_bit_mc_13_out_lt), .A(A[19]),
    .B(B[19]));
  _1_bit_MC u_1_bit_mc_14 (
    .in_gt(n1_bit_mc_11_out_gt), .in_eq(n1_bit_mc_11_out_eq), .in_lt(n1_bit_mc_11_out_lt),
    .out_gt(n1_bit_mc_14_out_gt), .out_eq(n1_bit_mc_14_out_eq), .out_lt(n1_bit_mc_14_out_lt), .A(A[20]),
    .B(B[20]));
  _1_bit_MC u_1_bit_mc_15 (
    .in_gt(n1_bit_mc_16_out_gt), .in_eq(n1_bit_mc_16_out_eq), .in_lt(n1_bit_mc_16_out_lt),
    .out_gt(n1_bit_mc_15_out_gt), .out_eq(n1_bit_mc_15_out_eq), .out_lt(n1_bit_mc_15_out_lt), .A(A[16]),
    .B(B[16]));
  _1_bit_MC u_1_bit_mc_16 (
    .in_gt(n1_bit_mc_12_out_gt), .in_eq(n1_bit_mc_12_out_eq), .in_lt(n1_bit_mc_12_out_lt),
    .out_gt(n1_bit_mc_16_out_gt), .out_eq(n1_bit_mc_16_out_eq), .out_lt(n1_bit_mc_16_out_lt), .A(A[17]),
    .B(B[17]));
  _1_bit_MC u_1_bit_mc_17 (
    .in_gt(n1_bit_mc_15_out_gt), .in_eq(n1_bit_mc_15_out_eq), .in_lt(n1_bit_mc_15_out_lt),
    .out_gt(n1_bit_mc_17_out_gt), .out_eq(n1_bit_mc_17_out_eq), .out_lt(n1_bit_mc_17_out_lt), .A(A[15]),
    .B(B[15]));
  _1_bit_MC u_1_bit_mc_18 (
    .in_gt(n1_bit_mc_19_out_gt), .in_eq(n1_bit_mc_19_out_eq), .in_lt(n1_bit_mc_19_out_lt),
    .out_gt(n1_bit_mc_18_out_gt), .out_eq(n1_bit_mc_18_out_eq), .out_lt(n1_bit_mc_18_out_lt), .A(A[13]),
    .B(B[13]));
  _1_bit_MC u_1_bit_mc_19 (
    .in_gt(n1_bit_mc_17_out_gt), .in_eq(n1_bit_mc_17_out_eq), .in_lt(n1_bit_mc_17_out_lt),
    .out_gt(n1_bit_mc_19_out_gt), .out_eq(n1_bit_mc_19_out_eq), .out_lt(n1_bit_mc_19_out_lt), .A(A[14]),
    .B(B[14]));
  _1_bit_MC u_1_bit_mc_20 (
    .in_gt(n1_bit_mc_21_out_gt), .in_eq(n1_bit_mc_21_out_eq), .in_lt(n1_bit_mc_21_out_lt),
    .out_gt(n1_bit_mc_20_out_gt), .out_eq(n1_bit_mc_20_out_eq), .out_lt(n1_bit_mc_20_out_lt), .A(A[11]),
    .B(B[11]));
  _1_bit_MC u_1_bit_mc_21 (
    .in_gt(n1_bit_mc_18_out_gt), .in_eq(n1_bit_mc_18_out_eq), .in_lt(n1_bit_mc_18_out_lt),
    .out_gt(n1_bit_mc_21_out_gt), .out_eq(n1_bit_mc_21_out_eq), .out_lt(n1_bit_mc_21_out_lt), .A(A[12]),
    .B(B[12]));
  _1_bit_MC u_1_bit_mc_22 (
    .in_gt(n1_bit_mc_20_out_gt), .in_eq(n1_bit_mc_20_out_eq), .in_lt(n1_bit_mc_20_out_lt),
    .out_gt(n1_bit_mc_22_out_gt), .out_eq(n1_bit_mc_22_out_eq), .out_lt(n1_bit_mc_22_out_lt), .A(A[10]),
    .B(B[10]));
  _1_bit_MC u_1_bit_mc_23 (
    .in_gt(n1_bit_mc_24_out_gt), .in_eq(n1_bit_mc_24_out_eq), .in_lt(n1_bit_mc_24_out_lt),
    .out_gt(n1_bit_mc_23_out_gt), .out_eq(n1_bit_mc_23_out_eq), .out_lt(n1_bit_mc_23_out_lt), .A(A[8]),
    .B(B[8]));
  _1_bit_MC u_1_bit_mc_24 (
    .in_gt(n1_bit_mc_22_out_gt), .in_eq(n1_bit_mc_22_out_eq), .in_lt(n1_bit_mc_22_out_lt),
    .out_gt(n1_bit_mc_24_out_gt), .out_eq(n1_bit_mc_24_out_eq), .out_lt(n1_bit_mc_24_out_lt), .A(A[9]),
    .B(B[9]));
  _1_bit_MC u_1_bit_mc_25 (
    .in_gt(n1_bit_mc_26_out_gt), .in_eq(n1_bit_mc_26_out_eq), .in_lt(n1_bit_mc_26_out_lt),
    .out_gt(n1_bit_mc_25_out_gt), .out_eq(n1_bit_mc_25_out_eq), .out_lt(n1_bit_mc_25_out_lt), .A(A[6]),
    .B(B[6]));
  _1_bit_MC u_1_bit_mc_26 (
    .in_gt(n1_bit_mc_23_out_gt), .in_eq(n1_bit_mc_23_out_eq), .in_lt(n1_bit_mc_23_out_lt),
    .out_gt(n1_bit_mc_26_out_gt), .out_eq(n1_bit_mc_26_out_eq), .out_lt(n1_bit_mc_26_out_lt), .A(A[7]),
    .B(B[7]));
  _1_bit_MC u_1_bit_mc_27 (
    .in_gt(n1_bit_mc_25_out_gt), .in_eq(n1_bit_mc_25_out_eq), .in_lt(n1_bit_mc_25_out_lt),
    .out_gt(n1_bit_mc_27_out_gt), .out_eq(n1_bit_mc_27_out_eq), .out_lt(n1_bit_mc_27_out_lt), .A(A[5]),
    .B(B[5]));
  _1_bit_MC u_1_bit_mc_28 (
    .in_gt(n1_bit_mc_30_out_gt), .in_eq(n1_bit_mc_30_out_eq), .in_lt(n1_bit_mc_30_out_lt),
    .out_gt(n1_bit_mc_28_out_gt), .out_eq(n1_bit_mc_28_out_eq), .out_lt(n1_bit_mc_28_out_lt), .A(A[3]),
    .B(B[3]));
  _1_bit_MC u_1_bit_mc_29 (
    .in_gt(n1_bit_mc_28_out_gt), .in_eq(n1_bit_mc_28_out_eq), .in_lt(n1_bit_mc_28_out_lt),
    .out_gt(n1_bit_mc_29_out_gt), .out_eq(n1_bit_mc_29_out_eq), .out_lt(n1_bit_mc_29_out_lt), .A(A[2]),
    .B(B[2]));
  _1_bit_MC u_1_bit_mc_30 (
    .in_gt(n1_bit_mc_27_out_gt), .in_eq(n1_bit_mc_27_out_eq), .in_lt(n1_bit_mc_27_out_lt),
    .out_gt(n1_bit_mc_30_out_gt), .out_eq(n1_bit_mc_30_out_eq), .out_lt(n1_bit_mc_30_out_lt), .A(A[4]),
    .B(B[4]));
  _1_bit_MC u_1_bit_mc_31 (
    .in_gt(n1_bit_mc_29_out_gt), .in_eq(n1_bit_mc_29_out_eq), .in_lt(n1_bit_mc_29_out_lt),
    .out_gt(n1_bit_mc_31_out_gt), .out_eq(n1_bit_mc_31_out_eq), .out_lt(n1_bit_mc_31_out_lt), .A(A[1]),
    .B(B[1]));
  _1_bit_MC u_1_bit_mc_32 (
    .in_gt(n1_bit_mc_31_out_gt), .in_eq(n1_bit_mc_31_out_eq), .in_lt(n1_bit_mc_31_out_lt), .out_gt(gt),
    .out_eq(e), .out_lt(lt), .A(A[0]), .B(B[0]));
endmodule

module _1_bit_MC (
  input  A,
  input  B,
  input  in_gt,
  input  in_eq,
  input  in_lt,
  output out_gt,
  output out_eq,
  output out_lt
);

  wire and_1_out, and_2_out, not_1_out, not_2_out, xnor_1_out;

  not not_1 (not_1_out, B);
  not not_2 (not_2_out, A);
  and and_1 (and_1_out, A, not_1_out, in_eq);
  xnor xnor_1 (xnor_1_out, A, B);
  and and_2 (and_2_out, not_2_out, B, in_eq);
  or or_1 (out_gt, and_1_out, in_gt);
  and and_3 (out_eq, xnor_1_out, in_eq);
  or or_2 (out_lt, and_2_out, in_lt);
endmodule

module Cond (
  input  [3:0] ifun,
  input  [2:0] CC,
  output condFlag
);

  wire and_1_out, and_2_out, and_3_out, and_4_out, and_5_out, and_6_out, and_7_out, decoder_1_out1,
       decoder_1_out2, decoder_1_out3, decoder_1_out4, decoder_1_out5, decoder_1_out6, not_1_out, not_2_out,
       not_3_out, not_4_out, or_1_out, or_2_out, or_3_out, or_4_out, or_5_out;

  Decoder #(.select(4)) decoder_1 (
    .out1(decoder_1_out1), .out2(decoder_1_out2), .out3(decoder_1_out3), .out4(decoder_1_out4),
    .out5(decoder_1_out5), .out6(decoder_1_out6), .sel(ifun));  // open: out0, out7, out8, out9, out10, out11, out12, out13, out14, out15, en
  or or_1 (or_1_out, CC[0], CC[1]);
  and and_1 (and_1_out, decoder_1_out3, CC[2]);
  and and_2 (and_2_out, decoder_1_out4, ~CC[2]);  // AND_Gate
  or or_2 (or_2_out, CC[0], CC[1]);
  or or_3 (or_3_out, CC[0], CC[1]);
  and and_3 (and_3_out, or_1_out, decoder_1_out2);
  or or_4 (or_4_out, CC[1], CC[1]);
  not not_1 (not_1_out, CC[2]);
  not not_2 (not_2_out, or_2_out);
  or or_5 (or_5_out, CC[2], not_3_out);
  not not_3 (not_3_out, or_3_out);
  not not_4 (not_4_out, or_4_out);
  and and_4 (and_4_out, not_4_out, not_1_out);
  and and_5 (and_5_out, decoder_1_out5, not_2_out);
  and and_6 (and_6_out, or_5_out, decoder_1_out1);
  and and_7 (and_7_out, decoder_1_out6, and_4_out);
  or or_6 (condFlag, and_6_out, and_3_out, and_1_out, and_2_out, and_7_out);

  // Notes on the sheet:
  //   workign with ifun and CC to make cond
endmodule
