// Logisim project Memory.circ as structural Verilog: 5 circuits, main circuit main
module main (
  input  [3:0] icode,
  input  [31:0] valE,
  input  [31:0] valA,
  input  [15:0] valP,
  output [31:0] valM,
  output [31:0] addr,
  output [31:0] data
);

  wire Clock_out, mem_control_1_read_ctrl_line, mem_control_1_write_ctrl_line;

  Clock Clock (.out(Clock_out));
  Mem__Control mem_control_1 (
    .in_1(icode), .Read_ctrl_line(mem_control_1_read_ctrl_line),
    .Write_ctrl_line(mem_control_1_write_ctrl_line));
  // Mem__Address mem_address_1: pin names not known; wires that end beside it: icode, valE, addr, valA
  mem_ex mem_ex_1 (
    .data(data), .addr(addr), .write_st(mem_control_1_write_ctrl_line),
    .read_ld(mem_control_1_read_ctrl_line), .Clock(Clock_out), .valM(valM));
  // Mem__Data mem_data_1: pin names not known; wires that end beside it: icode, valA, data, valP
endmodule

// Ctrl
module Mem__Control (
  input  [3:0] in_1,
  output Read_ctrl_line,
  output Write_ctrl_line
);

  and and_1 (Read_ctrl_line, ~in_1[0], in_1[1], ~in_1[2], ~in_1[3]);  // AND_Gate
  and and_2 (Write_ctrl_line, in_1[0], in_1[1], ~in_1[2], ~in_1[3]);  // AND_Gate
endmodule

module Mem__Address (
  input  [3:0] icode,
  input  [31:0] ValE,
  output [31:0] addr
);

  wire and_1_out;

  and and_1 (and_1_out, icode[1], ~icode[2], ~icode[3]);  // AND_Gate
  Multiplexer #(.width(32)) multiplexer_1 (.in1(ValE), .out(addr), .sel(and_1_out));  // open: in0, en
endmodule

module Mem__Data (
  input  [31:0] ValA,
  input  [3:0] icode,
  output [31:0] data
);

  wire and_1_out;

  and and_1 (and_1_out, icode[0], icode[1], ~icode[2], ~icode[3]);  // AND_Gate
  Multiplexer #(.width(32)) multiplexer_1 (.in1(ValA), .out(data), .sel(and_1_out));  // open: in0, en
endmodule

// Data Memory
module mem_ex (
  input  [31:0] data,
  input  [31:0] addr,
  input  write_st,
  input  read_ld,
  input  Clock,
  output [31:0] valM
);

  wire and_1_out, and_2_out, not_1_out;
  wire [7:0] counter_1_q;
  wire [31:0] controlled_buffer_1_out;

  assign controlled_buffer_1_out = write_st ? data : 32'bz;  // Controlled_Buffer controlled_buffer_1
  Counter counter_1 (.Q(counter_1_q), .clk(Clock), .clr(and_2_out));  // open: load, D, count, carry
  and and_1 (and_1_out, counter_1_q[0], ~counter_1_q[1], counter_1_q[2], ~counter_1_q[3]);  // AND_Gate
  and and_2 (and_2_out, ~counter_1_q[0], counter_1_q[1], counter_1_q[2], ~counter_1_q[3]);  // AND_Gate
  not not_1 (not_1_out, write_st);
  RAM #(.addrWidth(24), .dataWidth(32)) ram_1 (
    .addr(addr[23:0]), .data(controlled_buffer_1_out), .clk(and_1_out), .ld(not_1_out));  // open: sel, clr
  assign valM = read_ld ? controlled_buffer_1_out : 32'bz;  // Controlled_Buffer controlled_buffer_2
endmodule
