// Logisim project CPUJumpCond.circ as structural Verilog: 1 circuit, main circuit main
module main (
  output [31:0] ValC,
  output [31:0] ValM,
  output [15:0] PC_Increment,
  output [31:0] ValE,
  output [3:0] icode,
  output [31:0] ValE_2,
  output [31:0] ValA,
  output [31:0] ValB,
  output [31:0] ValM_2,
  output [31:0] ValE_3,
  output [3:0] ifun,
  output [31:0] ValC_2,
  output [3:0] icode_2,
  output [3:0] dstE,
  output [3:0] rA,
  output [3:0] rB,
  output [3:0] dstM,
  output [3:0] srcA,
  output [3:0] srcB
);

  wire clock_1_out, cond_1_condflag, fetch_unit_1_need_rgs, fetch_unit_1_need_valc,
       mem_control_1_read_ctrl_line, mem_control_1_write_ctrl_line, set_cc_1_cc;
  wire [2:0] alu_1_out_6, cc_1_out_3;
  wire [3:0] alu_fun_1_out_3;
  wire [15:0] newnewpc_1_new_pc, pc_1_out;
  wire [31:0] alua_1_out_4, alub_1_out_3, mem_address_1_addr, mem_data_1_data, undriven;

  Clock clock_1 (.out(clock_1_out));
  Fetch_Unit fetch_unit_1 (
    .Address_PC(pc_1_out), .icode(icode), .ifun(ifun), .rA(rA), .rB(rB), .valC(ValC),
    .need_Rgs(fetch_unit_1_need_rgs), .need_valC(fetch_unit_1_need_valc), .Clock(clock_1_out));
  Cond cond_1 (.ifun(ifun), .CC(cc_1_out_3), .condFlag(cond_1_condflag));
  CC cc_1 (.CC(alu_1_out_6), .setCC(set_cc_1_cc), .out_3(cc_1_out_3));
  set_CC set_cc_1 (.CC(set_cc_1_cc), .icode(icode));
  ALUA alua_1 (.out_4(alua_1_out_4), .icode(icode), .ValC(ValC), .ValA(ValA));
  PC pc_1 (.Clock(clock_1_out), .in(newnewpc_1_new_pc), .out(pc_1_out));
  Mem__Control mem_control_1 (
    .in_1(icode), .Read_ctrl_line(mem_control_1_read_ctrl_line),
    .Write_ctrl_line(mem_control_1_write_ctrl_line));
  mem_ex mem_ex_1 (
    .data(mem_data_1_data), .addr(mem_address_1_addr), .write_st(mem_control_1_write_ctrl_line),
    .read_ld(mem_control_1_read_ctrl_line), .Clock(clock_1_out), .valM(ValM));
  Mem__Address mem_address_1 (.icode(icode), .addr(mem_address_1_addr), .ValE(ValE));
  ALU alu_1 (
    .ALU_fun(alu_fun_1_out_3), .ALUA(alua_1_out_4), .ALUB(alub_1_out_3), .ValE(ValE), .Clock(clock_1_out),
    .out_6(alu_1_out_6));
  ALUB alub_1 (.out_3(alub_1_out_3), .icode(icode), .ValB(ValB));
  newNewPC newnewpc_1 (
    .iCode(icode), .Clock(clock_1_out), .Cnd(cond_1_condflag), .valC(ValC), .new_PC(newnewpc_1_new_pc),
    .valM(undriven), .valP(PC_Increment));
  Mem__Data mem_data_1 (.icode(icode), .data(mem_data_1_data), .ValA(ValA));
  ALU_fun alu_fun_1 (.out_3(alu_fun_1_out_3), .icode(icode), .ifun(ifun));
  PC_Increment pc_increment_1 (
    .valP(PC_Increment), .in_3(pc_1_out), .needValC(fetch_unit_1_need_valc),
    .need_regId(fetch_unit_1_need_rgs));
  Register_File register_file_1 (
    .W_Data___ValM(ValM), .W_Addr___DestM(dstM), .W_Data2___ValE(ValE), .W_Addr___DestE(dstE), .ValA(ValA),
    .ValB(ValB), .R_Addr___SrcB(srcB), .R_Addr___SrcA(srcA), .icode(icode), .Clock(clock_1_out));
  dstE dste_1 (.out_3(dstE), .icode(icode), .rB(rB));
  dstM dstm_1 (.out_3(dstM), .icode(icode), .rB(rA));
  srcA srca_1 (.out_3(srcA), .icode(icode), .rA(rA));
  srcB srcb_1 (.icode(icode), .out_3(srcB), .rB(rB));

  assign icode_2 = icode;
  assign ValC_2 = ValC;
  assign ValE_2 = ValE;
  assign ValE_3 = ValE;
  assign ValM_2 = ValM;

  // Notes on the sheet:
  //   icode
  //   rA
  //   rB
  //   condition code flags
  //   Bit 0: overflow
  //   Bit 1: Negative
  //   Bit 2: Zero
  //   ifun values
  //   0000 = Add
  //   0001 = Multiply
  //   0010 = Subtract
  //   0011 = AND
  //   0100 = OR
  //   icode
  //   0100 = OPL
  //   0101 = jmp
  //   0110 = jxx
endmodule
